// Logisim project seq_circuit.circ as structural Verilog: 1 circuit, main circuit main
// c
module main (
  input  x,
  input  s,
  input  y,
  input  Q_prime
);

  wire and_1_out, and_2_out, clock_1_out, nand_1_out, nand_2_out, nand_3_out, nand_4_out, nand_5_out,
       nand_6_out, or_1_out, or_2_out, xor_1_out, xor_2_out;

  Clock clock_1 (.out(clock_1_out));
  and and_1 (and_1_out, x, y);
  xor xor_1 (xor_1_out, x, y);
  nand nand_1 (nand_1_out, nand_4_out, nand_2_out);
  nand nand_2 (nand_2_out, nand_1_out, clock_1_out);
  nand nand_3 (nand_3_out, nand_2_out, clock_1_out, nand_4_out);
  nand nand_4 (nand_4_out, nand_3_out, or_2_out);
  xor xor_2 (xor_2_out, xor_1_out, nand_5_out);
  and and_2 (and_2_out, xor_1_out, nand_5_out);
  or or_1 (or_1_out, and_2_out, and_1_out);
  nand nand_5 (nand_5_out, nand_2_out, nand_6_out);
  nand nand_6 (nand_6_out, nand_5_out, nand_3_out);
  buf or_2 (or_2_out, or_1_out);  // OR_Gate

  // Notes on the sheet:
  //   D
  //   S
  //   R
  //   Q
  //   C
endmodule
